// Digital circuit 8-Bit ALU.dig as structural Verilog
module _8_Bit_ALU (
  input  [7:0] A,
  input  [7:0] B,
  input  SUB,
  output [7:0] OUT,
  output OF_UF
);

  wire _8_bit_adder_1_co;
  wire [7:0] _8_bit_inverter_1_out;

  _8_Bit_Inverter _8_bit_inverter_1 (.IN(B), .INV(SUB), .OUT(_8_bit_inverter_1_out));
  _8_Bit_Adder _8_bit_adder_1 (.CI(SUB), .A(A), .B(_8_bit_inverter_1_out), .S(OUT), .CO(_8_bit_adder_1_co));
  xor xor_1 (OF_UF, _8_bit_adder_1_co, SUB);

  // Notes on the sheet:
  //   OF_UF: overflow/underflow indicator
  //   SUB: 0 for addition and 1 for subtraction
endmodule
