// Digital circuit 8-Bit Inverter.dig as structural Verilog
module _8_Bit_Inverter (
  input  [7:0] IN,
  input  INV,
  output [7:0] OUT
);

  xor xor_1 (OUT[0], IN[0], INV);
  xor xor_2 (OUT[1], IN[1], INV);
  xor xor_3 (OUT[2], IN[2], INV);
  xor xor_4 (OUT[3], IN[3], INV);
  xor xor_5 (OUT[4], IN[4], INV);
  xor xor_6 (OUT[5], IN[5], INV);
  xor xor_7 (OUT[6], IN[6], INV);
  xor xor_8 (OUT[7], IN[7], INV);
endmodule
