// Digital circuit 8-Bit Latch Level-Triggered Clearable.dig as structural Verilog
module _8_Bit_Latch_Level_Triggered_Clearable (
  input  [7:0] D,
  input  Clk,
  input  Clr,
  output [7:0] Q
);

  D_Flip_Flop_Level_Triggered_Clearable d_flip_flop_level_triggered_clearable_1 (
    .D(D[0]), .Clk(Clk), .Clr(Clr), .Q(Q[0]));  // open: Q_2
  D_Flip_Flop_Level_Triggered_Clearable d_flip_flop_level_triggered_clearable_2 (
    .D(D[1]), .Clk(Clk), .Clr(Clr), .Q(Q[1]));  // open: Q_2
  D_Flip_Flop_Level_Triggered_Clearable d_flip_flop_level_triggered_clearable_3 (
    .D(D[2]), .Clk(Clk), .Clr(Clr), .Q(Q[2]));  // open: Q_2
  D_Flip_Flop_Level_Triggered_Clearable d_flip_flop_level_triggered_clearable_4 (
    .D(D[3]), .Clk(Clk), .Clr(Clr), .Q(Q[3]));  // open: Q_2
  D_Flip_Flop_Level_Triggered_Clearable d_flip_flop_level_triggered_clearable_5 (
    .D(D[4]), .Clk(Clk), .Clr(Clr), .Q(Q[4]));  // open: Q_2
  D_Flip_Flop_Level_Triggered_Clearable d_flip_flop_level_triggered_clearable_6 (
    .D(D[5]), .Clk(Clk), .Clr(Clr), .Q(Q[5]));  // open: Q_2
  D_Flip_Flop_Level_Triggered_Clearable d_flip_flop_level_triggered_clearable_7 (
    .D(D[6]), .Clk(Clk), .Clr(Clr), .Q(Q[6]));  // open: Q_2
  D_Flip_Flop_Level_Triggered_Clearable d_flip_flop_level_triggered_clearable_8 (
    .D(D[7]), .Clk(Clk), .Clr(Clr), .Q(Q[7]));  // open: Q_2

  // Notes on the sheet:
  //   Clk: clock
  //   Clr: clear
endmodule
