// Digital circuit 8-Bit Latch Level-Triggered.dig as structural Verilog
module _8_Bit_Latch_Level_Triggered (
  input  [7:0] D,
  input  Clk,
  output [7:0] Q
);

  // D_Flip_Flop_Level_Triggered d_flip_flop_level_triggered_1: pin names not known; wires that end beside it: D[0], Clk, Q[0]
  // D_Flip_Flop_Level_Triggered d_flip_flop_level_triggered_2: pin names not known; wires that end beside it: D[1], Clk, Q[1]
  // D_Flip_Flop_Level_Triggered d_flip_flop_level_triggered_3: pin names not known; wires that end beside it: D[2], Clk, Q[2]
  // D_Flip_Flop_Level_Triggered d_flip_flop_level_triggered_4: pin names not known; wires that end beside it: D[3], Clk, Q[3]
  // D_Flip_Flop_Level_Triggered d_flip_flop_level_triggered_5: pin names not known; wires that end beside it: D[4], Clk, Q[4]
  // D_Flip_Flop_Level_Triggered d_flip_flop_level_triggered_6: pin names not known; wires that end beside it: D[5], Clk, Q[5]
  // D_Flip_Flop_Level_Triggered d_flip_flop_level_triggered_7: pin names not known; wires that end beside it: D[6], Clk, Q[6]
  // D_Flip_Flop_Level_Triggered d_flip_flop_level_triggered_8: pin names not known; wires that end beside it: D[7], Clk, Q[7]
endmodule
