// Digital circuit 8-Bit Latch.dig as structural Verilog
module _8_Bit_Latch (
  input  [7:0] D,
  input  Clk,
  output [7:0] Q
);

  D_Flip_Flop d_flip_flop_1 (.Data(D[0]), .Clock(Clk), .Q(Q[0]));  // open: Q_2
  D_Flip_Flop d_flip_flop_2 (.Data(D[1]), .Clock(Clk), .Q(Q[1]));  // open: Q_2
  D_Flip_Flop d_flip_flop_3 (.Data(D[2]), .Clock(Clk), .Q(Q[2]));  // open: Q_2
  D_Flip_Flop d_flip_flop_4 (.Data(D[3]), .Clock(Clk), .Q(Q[3]));  // open: Q_2
  D_Flip_Flop d_flip_flop_5 (.Data(D[4]), .Clock(Clk), .Q(Q[4]));  // open: Q_2
  D_Flip_Flop d_flip_flop_6 (.Data(D[5]), .Clock(Clk), .Q(Q[5]));  // open: Q_2
  D_Flip_Flop d_flip_flop_7 (.Data(D[6]), .Clock(Clk), .Q(Q[6]));  // open: Q_2
  D_Flip_Flop d_flip_flop_8 (.Data(D[7]), .Clock(Clk), .Q(Q[7]));  // open: Q_2
endmodule
