// Digital circuit 8-Bit Ripple Counter.dig as structural Verilog
module _8_Bit_Ripple_Counter (
  input  clk,
  input  Clr,
  input  Pre,
  output Q0,
  output Q1,
  output Q2,
  output Q3,
  output Q4,
  output Q5,
  output Q6,
  output Q7
);

  wire d_flip_flop_edge_triggered_preset_clear_1_q_2, d_flip_flop_edge_triggered_preset_clear_2_q_2,
       d_flip_flop_edge_triggered_preset_clear_3_q_2, d_flip_flop_edge_triggered_preset_clear_4_q_2,
       d_flip_flop_edge_triggered_preset_clear_5_q_2, d_flip_flop_edge_triggered_preset_clear_6_q_2,
       d_flip_flop_edge_triggered_preset_clear_7_q_2, d_flip_flop_edge_triggered_preset_clear_8_q_2;

  D_Flip_Flop_Edge_Triggered_Preset_Clear d_flip_flop_edge_triggered_preset_clear_1 (
    .D(d_flip_flop_edge_triggered_preset_clear_1_q_2), .Clk(clk), .Clr(Clr), .Pre(Pre), .Q(Q0),
    .Q_2(d_flip_flop_edge_triggered_preset_clear_1_q_2));
  D_Flip_Flop_Edge_Triggered_Preset_Clear d_flip_flop_edge_triggered_preset_clear_2 (
    .D(d_flip_flop_edge_triggered_preset_clear_2_q_2), .Clk(d_flip_flop_edge_triggered_preset_clear_1_q_2),
    .Clr(Clr), .Pre(Pre), .Q(Q1), .Q_2(d_flip_flop_edge_triggered_preset_clear_2_q_2));
  D_Flip_Flop_Edge_Triggered_Preset_Clear d_flip_flop_edge_triggered_preset_clear_3 (
    .D(d_flip_flop_edge_triggered_preset_clear_3_q_2), .Clk(d_flip_flop_edge_triggered_preset_clear_2_q_2),
    .Clr(Clr), .Pre(Pre), .Q(Q2), .Q_2(d_flip_flop_edge_triggered_preset_clear_3_q_2));
  D_Flip_Flop_Edge_Triggered_Preset_Clear d_flip_flop_edge_triggered_preset_clear_4 (
    .D(d_flip_flop_edge_triggered_preset_clear_4_q_2), .Clk(d_flip_flop_edge_triggered_preset_clear_3_q_2),
    .Clr(Clr), .Pre(Pre), .Q(Q3), .Q_2(d_flip_flop_edge_triggered_preset_clear_4_q_2));
  D_Flip_Flop_Edge_Triggered_Preset_Clear d_flip_flop_edge_triggered_preset_clear_5 (
    .D(d_flip_flop_edge_triggered_preset_clear_5_q_2), .Clk(d_flip_flop_edge_triggered_preset_clear_4_q_2),
    .Clr(Clr), .Pre(Pre), .Q(Q4), .Q_2(d_flip_flop_edge_triggered_preset_clear_5_q_2));
  D_Flip_Flop_Edge_Triggered_Preset_Clear d_flip_flop_edge_triggered_preset_clear_6 (
    .D(d_flip_flop_edge_triggered_preset_clear_6_q_2), .Clk(d_flip_flop_edge_triggered_preset_clear_5_q_2),
    .Clr(Clr), .Pre(Pre), .Q(Q5), .Q_2(d_flip_flop_edge_triggered_preset_clear_6_q_2));
  D_Flip_Flop_Edge_Triggered_Preset_Clear d_flip_flop_edge_triggered_preset_clear_7 (
    .D(d_flip_flop_edge_triggered_preset_clear_7_q_2), .Clk(d_flip_flop_edge_triggered_preset_clear_6_q_2),
    .Clr(Clr), .Pre(Pre), .Q(Q6), .Q_2(d_flip_flop_edge_triggered_preset_clear_7_q_2));
  D_Flip_Flop_Edge_Triggered_Preset_Clear d_flip_flop_edge_triggered_preset_clear_8 (
    .D(d_flip_flop_edge_triggered_preset_clear_8_q_2), .Clk(d_flip_flop_edge_triggered_preset_clear_7_q_2),
    .Clr(Clr), .Pre(Pre), .Q(Q7), .Q_2(d_flip_flop_edge_triggered_preset_clear_8_q_2));

  // Notes on the sheet:
  //   Clr: clear
  //   Pre: preset
endmodule
