// Digital circuit 2-Bit Adder.dig as structural Verilog
module _2_Bit_Adder (
  input  CI,
  input  [1:0] A,
  input  [1:0] B,
  output [1:0] S,
  output CO
);

  wire full_adder_1_co;

  Full_Adder full_adder_1 (.CI(CI), .A(A[0]), .B(B[0]), .S(S[0]), .CO(full_adder_1_co));
  Full_Adder full_adder_2 (.CI(full_adder_1_co), .A(A[1]), .B(B[1]), .S(S[1]), .CO(CO));
endmodule
