// Digital circuit 4-Bit Adder.dig as structural Verilog
module _4_Bit_Adder (
  input  CI,
  input  [3:0] A,
  input  [3:0] B,
  output [3:0] S,
  output CO
);

  wire _2_bit_adder_1_co;

  _2_Bit_Adder _2_bit_adder_1 (.CI(CI), .A(A[1:0]), .B(B[1:0]), .S(S[1:0]), .CO(_2_bit_adder_1_co));
  _2_Bit_Adder _2_bit_adder_2 (.CI(_2_bit_adder_1_co), .A(A[3:2]), .B(B[3:2]), .S(S[3:2]), .CO(CO));
endmodule
