// Digital circuit 8-Bit Adder.dig as structural Verilog
module _8_Bit_Adder (
  input  CI,
  input  [7:0] A,
  input  [7:0] B,
  output [7:0] S,
  output CO
);

  wire _4_bit_adder_1_co;

  _4_Bit_Adder _4_bit_adder_1 (.CI(CI), .A(A[3:0]), .B(B[3:0]), .S(S[3:0]), .CO(_4_bit_adder_1_co));
  _4_Bit_Adder _4_bit_adder_2 (.CI(_4_bit_adder_1_co), .A(A[7:4]), .B(B[7:4]), .S(S[7:4]), .CO(CO));
endmodule
