// Digital circuit Full Adder.dig as structural Verilog
module Full_Adder (
  input  CI,
  input  A,
  input  B,
  output S,
  output CO
);

  wire half_adder_1_co, half_adder_1_s, half_adder_2_co;

  Half_Adder half_adder_1 (.A(A), .B(B), .S(half_adder_1_s), .CO(half_adder_1_co));
  Half_Adder half_adder_2 (.A(CI), .B(half_adder_1_s), .S(S), .CO(half_adder_2_co));
  or or_1 (CO, half_adder_2_co, half_adder_1_co);
endmodule
