// Digital circuit 3-to-8 Decoder.dig as structural Verilog
module _3_to_8_Decoder (
  input  Data,
  input  S0,
  input  S1,
  input  S2,
  output O7,
  output O6,
  output O5,
  output O4,
  output O3,
  output O2,
  output O1,
  output O0
);

  and and_1 (O7, Data, S0, S1, S2);
  and and_2 (O6, Data, ~S0, S1, S2);  // And
  and and_3 (O5, Data, S0, ~S1, S2);  // And
  and and_4 (O4, Data, ~S0, ~S1, S2);  // And
  and and_5 (O3, Data, S0, S1, ~S2);  // And
  and and_6 (O2, Data, ~S0, S1, ~S2);  // And
  and and_7 (O1, Data, S0, ~S1, ~S2);  // And
  and and_8 (O0, Data, ~S0, ~S1, ~S2);  // And
endmodule
