// Digital circuit D Flip-Flop Edge-Triggered Clearable.dig as structural Verilog
module D_Flip_Flop_Edge_Triggered_Clearable (
  input  D,
  input  Clk,
  input  Clr,
  output Q,
  output Q_2
);

  wire and_1_out, not_1_out, not_2_out, or_1_out, or_2_out, r_s_flip_flop_clocked_1_q,
       r_s_flip_flop_clocked_1_q_2;

  not not_1 (not_1_out, D);
  not not_2 (not_2_out, Clk);
  R_S_Flip_Flop_Clocked r_s_flip_flop_clocked_1 (
    .R(D), .S(not_1_out), .Clk(not_2_out), .Q(r_s_flip_flop_clocked_1_q), .Q_2(r_s_flip_flop_clocked_1_q_2));
  or or_1 (or_1_out, Clk, Clr);
  or or_2 (or_2_out, Clr, r_s_flip_flop_clocked_1_q);
  and and_1 (and_1_out, r_s_flip_flop_clocked_1_q_2, ~Clr);  // And
  R_S_Flip_Flop_Clocked r_s_flip_flop_clocked_2 (.R(or_2_out), .S(and_1_out), .Clk(or_1_out), .Q(Q), .Q_2(Q_2));

  // Notes on the sheet:
  //   D: data
  //   Clk: clock
  //   Clr: clear
endmodule
