// Digital circuit D Flip-Flop Edge-Triggered.dig as structural Verilog
module D_Flip_Flop_Edge_Triggered (
  input  D,
  input  Clk,
  output Q,
  output Q_2
);

  wire not_1_out, not_2_out, r_s_flip_flop_clocked_1_q, r_s_flip_flop_clocked_1_q_2;

  not not_1 (not_1_out, D);
  not not_2 (not_2_out, Clk);
  R_S_Flip_Flop_Clocked r_s_flip_flop_clocked_1 (
    .R(D), .S(not_1_out), .Clk(not_2_out), .Q(r_s_flip_flop_clocked_1_q), .Q_2(r_s_flip_flop_clocked_1_q_2));
  R_S_Flip_Flop_Clocked r_s_flip_flop_clocked_2 (
    .R(r_s_flip_flop_clocked_1_q), .S(r_s_flip_flop_clocked_1_q_2), .Clk(Clk), .Q(Q), .Q_2(Q_2));

  // Notes on the sheet:
  //   D: data
  //   Clk: clock
endmodule
