// Digital circuit D Flip-Flop Level-Triggered Clearable.dig as structural Verilog
module D_Flip_Flop_Level_Triggered_Clearable (
  input  D,
  input  Clk,
  input  Clr,
  output Q,
  output Q_2
);

  wire and_1_out, and_2_out, not_1_out, or_1_out;

  not not_1 (not_1_out, D);
  and and_1 (and_1_out, not_1_out, Clk);
  and and_2 (and_2_out, D, Clk);
  or or_1 (or_1_out, Clr, and_1_out);
  R_S_Flip_Flop r_s_flip_flop_1 (.R(or_1_out), .S(and_2_out), .Q(Q), .Q_2(Q_2));

  // Notes on the sheet:
  //   D: data
  //   Clk: clock
  //   Clr: clear
endmodule
