// Digital circuit R-S Flip-Flop Clocked.dig as structural Verilog
module R_S_Flip_Flop_Clocked (
  input  R,
  input  S,
  input  Clk,
  output Q,
  output Q_2
);

  wire and_1_out, and_2_out;

  and and_1 (and_1_out, R, Clk);
  and and_2 (and_2_out, Clk, S);
  nor nor_1 (Q, and_1_out, Q_2);
  nor nor_2 (Q_2, Q, and_2_out);

  // Notes on the sheet:
  //   R: reset Q to zero
  //   S: set Q to 1
  //   Clk: clock
endmodule
