// Digital circuit R-S Flip-Flop.dig as structural Verilog
module R_S_Flip_Flop (
  input  R,
  input  S,
  output Q,
  output Q_2
);

  nor nor_1 (Q, R, Q_2);
  nor nor_2 (Q_2, Q, S);

  // Notes on the sheet:
  //   R: reset Q to zero
  //   S: set Q to 1
endmodule
