// Digital circuit 1-Bit Selector.dig as structural Verilog
module _1_Bit_Selector (
  input  A,
  input  B,
  input  Sel,
  output Out
);

  wire and_1_out, and_2_out;

  and and_1 (and_1_out, A, ~Sel);  // And
  and and_2 (and_2_out, B, Sel);
  or or_1 (Out, and_1_out, and_2_out);
endmodule
