// Digital circuit 8-Bit Selector.dig as structural Verilog
module _8_Bit_Selector (
  input  [7:0] A,
  input  [7:0] B,
  input  Sel,
  output [7:0] Out
);

  _1_Bit_Selector _1_bit_selector_1 (.A(A[0]), .B(B[0]), .Sel(Sel), .Out(Out[0]));
  _1_Bit_Selector _1_bit_selector_2 (.A(A[1]), .B(B[1]), .Sel(Sel), .Out(Out[1]));
  _1_Bit_Selector _1_bit_selector_3 (.A(A[2]), .B(B[2]), .Sel(Sel), .Out(Out[2]));
  _1_Bit_Selector _1_bit_selector_4 (.A(A[3]), .B(B[3]), .Sel(Sel), .Out(Out[3]));
  _1_Bit_Selector _1_bit_selector_5 (.A(A[4]), .B(B[4]), .Sel(Sel), .Out(Out[4]));
  _1_Bit_Selector _1_bit_selector_6 (.A(A[5]), .B(B[5]), .Sel(Sel), .Out(Out[5]));
  _1_Bit_Selector _1_bit_selector_7 (.A(A[6]), .B(B[6]), .Sel(Sel), .Out(Out[6]));
  _1_Bit_Selector _1_bit_selector_8 (.A(A[7]), .B(B[7]), .Sel(Sel), .Out(Out[7]));
endmodule
